# Fritzing sketch Vex button (saved by Fritzing 0.9.2b)
breadboards: 1

parts:
  S1 = Round Pushbutton
  Part1 = Arduino Uno (Rev3)

nets:
  N1: S1.leg0, Part1.D3_PWM
  N2: S1.leg1, Part1.GND

notes:
  vex button
  3 pins

// code stored in the sketch: button.ino
const int ledPin = 13;
const int buttonPin = 3;
int buttonState = 0;

void setup()
{
  pinMode(ledPin, OUTPUT);
  pinMode(buttonPin, INPUT);
}
void loop()
{
  buttonState = digitalRead(buttonPin);
  if(buttonState == HIGH)
    digitalWrite(ledPin, HIGH);
  else 
    digitalWrite(ledPin, LOW);
}
